// Digital circuit controlUnit.dig as structural Verilog
// generates control signals for datapath
module controlUnit (
  input  clock,
  input  reset,
  input  [15:0] dIn,
  input  alt,
  input  NE,
  input  GE,
  output wr,
  output rd,
  output sign,
  output word,
  output sub,
  output \logic ,
  output [1:0] logSelect,
  output [11:0] topImm,
  output even,
  output const2,
  output selImm,
  output selConst,
  output Azero,
  output we,
  output [3:0] Rw,
  output [3:0] Ra,
  output [3:0] Rb,
  output selRd,
  output selAddr
);

  wire [11:0] multiplexer_1_out;
  wire [11:4] undriven;
  wire [15:0] IR_q;

  Multiplexer multiplexer_1 (.in_0(IR_q[4]), .in_1(1'b0), .out(multiplexer_1_out[0]));  // open: sel
  Register #(.Bits(16)) IR (.D(dIn), .C(clock), .Q(IR_q));  // open: en
  D_FF #(.Bits(12)) IM (.D(multiplexer_1_out), .C(clock), .Q(topImm));  // open: nQ
  // Pins of 1 and 12 bits meet at multiplexer_1_out
  // Pins of 4 and 12 bits meet at {undriven, IR_q[3:0]}
  // Pins of 1 and 12 bits meet at IR_q[15:4]
  // Pins of 1 and 12 bits meet at {12{1'b0}}

  // Notes on the sheet:
  //   clock: controls internal registers
  //   reset: when high forces the PC to 0x0000
  //   dIn: data from memory
  //   alt: immediate value indicates alternative instruction in lowest bit
  //   NE: A ~= B
  //   GE: A >= B
  //   wr: memory write cycle
  //   rd: memory read cycle
  //   sign: not LBU
  //   word: not SB, LB or LBU
  //   sub: change addition to subtraction
  //   logic: select logic operation instead of addition
  //   logSelect: selects between shift right, AND, OR, XOR
  //   topImm: saved from prefix instruction
  //   even: forces bottom bit of immediate to 0
  //   const2: changes constant from 0 to 2
  //   selImm: B is immediate
  //   selConst: B is a constant
  //   Azero: force A to 0
  //   we: updates register Rw
  //   Rw: register to be written
  //   Ra: first register to read
  //   Rb: second register to read
  //   selRd: selects betweenALU result and memory for write back
  //   selAddr: selects between ALU result and Ra as the address to memory
endmodule
